// Logisim project bcdtosevensegment.circ as structural Verilog
module bcdtosevensegment (
  input  b3,
  input  b2,
  input  b1,
  input  b0,
  output a,
  output b,
  output c,
  output d,
  output e,
  output f,
  output g,
  output dp
);

  wire and_1_out, and_2_out, and_3_out, and_4_out, and_5_out, and_6_out, and_7_out, and_8_out, and_9_out,
       and_10_out, and_11_out, and_12_out, and_13_out, and_14_out, and_15_out, and_16_out, and_17_out,
       and_18_out, and_19_out, and_20_out, and_21_out, and_22_out, and_23_out, and_24_out, and_25_out,
       and_26_out, and_27_out, and_28_out, not_1_out, not_2_out, not_3_out, not_4_out, not_5_out, not_6_out,
       not_7_out, not_8_out, not_9_out, not_10_out, not_11_out, not_12_out, not_13_out, not_14_out,
       not_15_out, not_16_out, not_17_out, not_18_out, not_19_out, not_20_out, not_21_out, not_22_out,
       not_23_out, not_24_out, not_25_out, not_26_out, not_27_out, not_28_out, not_29_out, not_30_out,
       not_31_out, not_32_out, not_33_out, not_34_out, not_35_out, not_36_out, not_37_out, not_38_out,
       not_39_out, not_40_out, not_41_out, not_42_out, not_43_out, not_44_out, not_45_out, not_46_out,
       not_47_out, not_48_out, not_49_out, not_50_out, not_51_out, not_52_out, not_53_out;

  not not_1 (not_1_out, b2);
  and and_1 (and_1_out, not_1_out, not_2_out);
  not not_2 (not_2_out, b0);
  not not_3 (not_3_out, b3);
  and and_2 (and_2_out, not_3_out, b1);
  not not_4 (not_4_out, b3);
  and and_3 (and_3_out, not_4_out, b2, b0);
  not not_5 (not_5_out, b2);
  and and_4 (and_4_out, b3, not_5_out, not_6_out);
  not not_6 (not_6_out, b1);
  not not_7 (not_7_out, b3);
  and and_5 (and_5_out, not_7_out, not_8_out, not_9_out);
  not not_8 (not_8_out, b1);
  not not_9 (not_9_out, b0);
  not not_10 (not_10_out, b2);
  and and_6 (and_6_out, not_10_out, not_11_out);
  not not_11 (not_11_out, b1);
  not not_12 (not_12_out, b2);
  and and_7 (and_7_out, not_12_out, not_13_out);
  not not_13 (not_13_out, b0);
  not not_14 (not_14_out, b3);
  and and_8 (and_8_out, not_14_out, b1, b0);
  not not_15 (not_15_out, b2);
  and and_9 (and_9_out, not_15_out, not_16_out);
  not not_16 (not_16_out, b1);
  not not_17 (not_17_out, b3);
  and and_10 (and_10_out, not_17_out, b0);
  not not_18 (not_18_out, b3);
  and and_11 (and_11_out, not_18_out, b2);
  not not_19 (not_19_out, b2);
  not not_20 (not_20_out, b0);
  not not_21 (not_21_out, b3);
  not not_22 (not_22_out, b2);
  not not_23 (not_23_out, b3);
  not not_24 (not_24_out, b0);
  not not_25 (not_25_out, b3);
  not not_26 (not_26_out, b1);
  not not_27 (not_27_out, b2);
  not not_28 (not_28_out, b1);
  not not_29 (not_29_out, b2);
  and and_12 (and_12_out, not_29_out, not_30_out);
  not not_30 (not_30_out, b0);
  not not_31 (not_31_out, b3);
  and and_13 (and_13_out, not_31_out, b1, not_32_out);
  not not_32 (not_32_out, b0);
  not not_33 (not_33_out, b3);
  and and_14 (and_14_out, not_33_out, not_34_out, not_35_out);
  not not_34 (not_34_out, b1);
  not not_35 (not_35_out, b0);
  not not_36 (not_36_out, b3);
  and and_15 (and_15_out, not_36_out, b2, not_37_out);
  not not_37 (not_37_out, b1);
  not not_38 (not_38_out, b3);
  and and_16 (and_16_out, not_38_out, b2, not_39_out);
  not not_39 (not_39_out, b0);
  not not_40 (not_40_out, b2);
  and and_17 (and_17_out, b3, not_40_out, not_41_out);
  not not_41 (not_41_out, b1);
  not not_42 (not_42_out, b2);
  and and_18 (and_18_out, b3, not_42_out, not_43_out);
  not not_43 (not_43_out, b0);
  not not_44 (not_44_out, b3);
  not not_45 (not_45_out, b2);
  and and_19 (and_19_out, not_44_out, not_45_out, b1);
  not not_46 (not_46_out, b3);
  and and_20 (and_20_out, not_46_out, b2, not_47_out);
  not not_47 (not_47_out, b1);
  not not_48 (not_48_out, b3);
  and and_21 (and_21_out, not_48_out, b2, not_49_out);
  not not_49 (not_49_out, b0);
  and and_22 (and_22_out, b3, not_50_out, not_51_out);
  not not_50 (not_50_out, b2);
  not not_51 (not_51_out, b1);
  not not_52 (not_52_out, b2);
  and and_23 (and_23_out, b3, not_52_out, not_53_out);
  not not_53 (not_53_out, b0);
  or or_1 (a, and_1_out, and_2_out, and_3_out, and_4_out);
  or or_2 (b, and_5_out, and_6_out, and_7_out, and_8_out);
  or or_3 (c, and_9_out, and_10_out, and_11_out);
  and and_24 (and_24_out, not_19_out, not_20_out);
  and and_25 (and_25_out, not_21_out, not_22_out, b1);
  and and_26 (and_26_out, not_23_out, b1, not_24_out);
  and and_27 (and_27_out, not_25_out, b2, not_26_out, b0);
  and and_28 (and_28_out, b3, not_27_out, not_28_out);
  or or_4 (e, and_12_out, and_13_out);
  or or_5 (f, and_14_out, and_15_out, and_16_out, and_17_out, and_18_out);
  or or_6 (g, and_19_out, and_20_out, and_21_out, and_22_out, and_23_out);
  or or_7 (d, and_24_out, and_25_out, and_26_out, and_27_out, and_28_out);

  assign dp = 1'b0;

  // Notes on the sheet:
  //   23CS081
endmodule

module display0to9 (
  input  [3:0] BCD_input
);

  wire bcdtosevensegment_1_a, bcdtosevensegment_1_b, bcdtosevensegment_1_c, bcdtosevensegment_1_d,
       bcdtosevensegment_1_dp, bcdtosevensegment_1_e, bcdtosevensegment_1_f, bcdtosevensegment_1_g;

  bcdtosevensegment bcdtosevensegment_1 (
    .b3(BCD_input[3]), .b2(BCD_input[2]), .b1(BCD_input[1]), .b0(BCD_input[0]), .a(bcdtosevensegment_1_a),
    .b(bcdtosevensegment_1_b), .c(bcdtosevensegment_1_c), .d(bcdtosevensegment_1_d),
    .e(bcdtosevensegment_1_e), .f(bcdtosevensegment_1_f), .g(bcdtosevensegment_1_g),
    .dp(bcdtosevensegment_1_dp));
  _7_Segment_Display u_7_segment_display_1 (
    .g(bcdtosevensegment_1_g), .f(bcdtosevensegment_1_f), .a(bcdtosevensegment_1_a),
    .b(bcdtosevensegment_1_b), .e(bcdtosevensegment_1_e), .d(bcdtosevensegment_1_d),
    .c(bcdtosevensegment_1_c), .dp(bcdtosevensegment_1_dp));

  // Notes on the sheet:
  //   23CS081
endmodule

module sevenbitbinarytobcd (
  input  b6,
  input  b5,
  input  b4,
  input  b3,
  input  b2,
  input  b1,
  input  b0,
  output bcd1_3,
  output bcd1_2,
  output bcd1_1,
  output bcd1_0,
  output bcd0_3,
  output bcd0_2,
  output bcd0_1,
  output bcd_0
);

  wire and_1_out, and_2_out, and_3_out, and_4_out, and_5_out, and_6_out, and_7_out, and_8_out, and_9_out,
       and_10_out, and_11_out, and_12_out, and_13_out, and_14_out, and_15_out, and_16_out, and_17_out,
       and_18_out, and_19_out, and_20_out, and_21_out, and_22_out, and_23_out, and_24_out, and_25_out,
       and_26_out, and_27_out, and_28_out, and_29_out, and_30_out, and_31_out, and_32_out, and_33_out,
       and_34_out, and_35_out, and_36_out, and_37_out, and_38_out, and_39_out, and_40_out, and_41_out,
       and_42_out, and_43_out, and_44_out, and_45_out, and_46_out, and_47_out, and_48_out, and_49_out,
       and_50_out, and_51_out, and_52_out, and_53_out, and_54_out, and_55_out, and_56_out, and_57_out,
       and_58_out, not_1_out, not_2_out, not_3_out, not_4_out, not_5_out, not_6_out, not_7_out, not_8_out,
       not_9_out, not_10_out, not_11_out, not_12_out, not_13_out, not_14_out, not_15_out, not_16_out,
       not_17_out, not_18_out, not_19_out, not_20_out, not_21_out, not_22_out, not_23_out, not_24_out,
       not_25_out, not_26_out, not_27_out, not_28_out, not_29_out, not_30_out, not_31_out, not_32_out,
       not_33_out, not_34_out, not_35_out, not_36_out, not_37_out, not_38_out, not_39_out, not_40_out,
       not_41_out, not_42_out, not_43_out, not_44_out, not_45_out, not_46_out, not_47_out, not_48_out,
       not_49_out, not_50_out, not_51_out, not_52_out, not_53_out, not_54_out, not_55_out, not_56_out,
       not_57_out, not_58_out, not_59_out, not_60_out, not_61_out, not_62_out, not_63_out, not_64_out,
       not_65_out, not_66_out, not_67_out, not_68_out, not_69_out, not_70_out, not_71_out, not_72_out,
       not_73_out, not_74_out, not_75_out, not_76_out, not_77_out, not_78_out, not_79_out, not_80_out,
       not_81_out, not_82_out, not_83_out, not_84_out, not_85_out, not_86_out, not_87_out, not_88_out,
       not_89_out, not_90_out, not_91_out, not_92_out, not_93_out, not_94_out, not_95_out, not_96_out,
       not_97_out, not_98_out, not_99_out, not_100_out, not_101_out, not_102_out, not_103_out, not_104_out,
       not_105_out, not_106_out, not_107_out, not_108_out, not_109_out, not_110_out, not_111_out,
       not_112_out, not_113_out, not_114_out, not_115_out;

  not not_1 (not_1_out, b5);
  not not_2 (not_2_out, b4);
  not not_3 (not_3_out, b6);
  not not_4 (not_4_out, b5);
  not not_5 (not_5_out, b6);
  not not_6 (not_6_out, b5);
  not not_7 (not_7_out, b6);
  not not_8 (not_8_out, b6);
  not not_9 (not_9_out, b4);
  not not_10 (not_10_out, b3);
  not not_11 (not_11_out, b5);
  not not_12 (not_12_out, b4);
  not not_13 (not_13_out, b5);
  not not_14 (not_14_out, b4);
  not not_15 (not_15_out, b5);
  not not_16 (not_16_out, b6);
  not not_17 (not_17_out, b5);
  not not_18 (not_18_out, b3);
  not not_19 (not_19_out, b2);
  not not_20 (not_20_out, b2);
  not not_21 (not_21_out, b4);
  not not_22 (not_22_out, b6);
  not not_23 (not_23_out, b5);
  not not_24 (not_24_out, b4);
  not not_25 (not_25_out, b2);
  not not_26 (not_26_out, b1);
  not not_27 (not_27_out, b6);
  not not_28 (not_28_out, b5);
  not not_29 (not_29_out, b3);
  not not_30 (not_30_out, b2);
  not not_31 (not_31_out, b6);
  not not_32 (not_32_out, b5);
  not not_33 (not_33_out, b1);
  not not_34 (not_34_out, b6);
  not not_35 (not_35_out, b4);
  not not_36 (not_36_out, b3);
  not not_37 (not_37_out, b2);
  not not_38 (not_38_out, b6);
  not not_39 (not_39_out, b5);
  not not_40 (not_40_out, b3);
  not not_41 (not_41_out, b2);
  not not_42 (not_42_out, b1);
  not not_43 (not_43_out, b6);
  not not_44 (not_44_out, b5);
  not not_45 (not_45_out, b2);
  and and_1 (and_1_out, b6, b4);
  or or_1 (bcd1_3, and_1_out, and_2_out);
  and and_2 (and_2_out, b6, b5);
  and and_3 (and_3_out, b5, b3);
  and and_4 (and_4_out, b5, b4);
  and and_5 (and_5_out, b6, not_1_out, not_2_out);
  and and_6 (and_6_out, not_3_out, not_4_out, b4, b2);
  and and_7 (and_7_out, not_5_out, not_6_out, b4, b3);
  and and_8 (and_8_out, not_7_out, b4, b3, b2);
  and and_9 (and_9_out, not_8_out, b5, not_9_out, not_10_out);
  not not_46 (not_46_out, b5);
  and and_10 (and_10_out, b6, not_46_out, not_47_out);
  not not_47 (not_47_out, b4);
  and and_11 (and_11_out, not_11_out, not_12_out, b3, b1);
  and and_12 (and_12_out, not_13_out, not_14_out, b3, b2);
  and and_13 (and_13_out, not_15_out, b3, b2, b1);
  and and_14 (and_14_out, not_16_out, not_17_out, b4, not_18_out, not_19_out);
  and and_15 (and_15_out, b5, not_48_out, not_49_out);
  not not_48 (not_48_out, b4);
  not not_49 (not_49_out, b3);
  and and_16 (and_16_out, b5, not_50_out, b1);
  not not_50 (not_50_out, b3);
  not not_51 (not_51_out, b3);
  and and_17 (and_17_out, b5, not_51_out, b2);
  and and_18 (and_18_out, b5, b4, b3, not_20_out);
  and and_19 (and_19_out, b6, not_21_out, b2, b1);
  and and_20 (and_20_out, b6, not_52_out, b3);
  not not_52 (not_52_out, b4);
  and and_21 (and_21_out, b6, b3, b1);
  and and_22 (and_22_out, b6, b3, b2);
  not not_53 (not_53_out, b4);
  not not_54 (not_54_out, b3);
  not not_55 (not_55_out, b3);
  not not_56 (not_56_out, b2);
  not not_57 (not_57_out, b1);
  not not_58 (not_58_out, b2);
  not not_59 (not_59_out, b4);
  not not_60 (not_60_out, b3);
  not not_61 (not_61_out, b1);
  not not_62 (not_62_out, b4);
  not not_63 (not_63_out, b2);
  not not_64 (not_64_out, b1);
  not not_65 (not_65_out, b6);
  not not_66 (not_66_out, b5);
  not not_67 (not_67_out, b4);
  not not_68 (not_68_out, b3);
  not not_69 (not_69_out, b6);
  not not_70 (not_70_out, b4);
  not not_71 (not_71_out, b6);
  not not_72 (not_72_out, b5);
  not not_73 (not_73_out, b2);
  not not_74 (not_74_out, b1);
  not not_75 (not_75_out, b6);
  not not_76 (not_76_out, b5);
  not not_77 (not_77_out, b2);
  not not_78 (not_78_out, b6);
  not not_79 (not_79_out, b2);
  not not_80 (not_80_out, b1);
  not not_81 (not_81_out, b4);
  not not_82 (not_82_out, b1);
  not not_83 (not_83_out, b3);
  not not_84 (not_84_out, b4);
  not not_85 (not_85_out, b3);
  not not_86 (not_86_out, b2);
  not not_87 (not_87_out, b1);
  not not_88 (not_88_out, b5);
  not not_89 (not_89_out, b4);
  not not_90 (not_90_out, b2);
  not not_91 (not_91_out, b4);
  not not_92 (not_92_out, b1);
  not not_93 (not_93_out, b3);
  not not_94 (not_94_out, b5);
  not not_95 (not_95_out, b4);
  not not_96 (not_96_out, b3);
  not not_97 (not_97_out, b2);
  not not_98 (not_98_out, b6);
  not not_99 (not_99_out, b5);
  not not_100 (not_100_out, b3);
  not not_101 (not_101_out, b5);
  not not_102 (not_102_out, b4);
  not not_103 (not_103_out, b1);
  not not_104 (not_104_out, b4);
  not not_105 (not_105_out, b3);
  not not_106 (not_106_out, b1);
  not not_107 (not_107_out, b3);
  not not_108 (not_108_out, b1);
  not not_109 (not_109_out, b4);
  not not_110 (not_110_out, b2);
  not not_111 (not_111_out, b1);
  not not_112 (not_112_out, b4);
  not not_113 (not_113_out, b1);
  not not_114 (not_114_out, b1);
  not not_115 (not_115_out, b3);
  or or_2 (bcd1_2, and_3_out, and_4_out, and_5_out);
  or or_3 (bcd1_1, and_6_out, and_7_out, and_8_out, and_9_out, and_10_out);
  and and_23 (and_23_out, not_22_out, not_23_out, not_24_out, b3, not_25_out, not_26_out);
  and and_24 (and_24_out, not_27_out, not_28_out, b4, not_29_out, not_30_out, b1);
  and and_25 (and_25_out, not_31_out, not_32_out, b4, b3, b2, not_33_out);
  and and_26 (and_26_out, b5, not_53_out, not_54_out, b2, b1);
  and and_27 (and_27_out, b5, b4, not_55_out, not_56_out, not_57_out);
  and and_28 (and_28_out, b5, b4, b3, not_58_out, b1);
  and and_29 (and_29_out, b6, not_59_out, not_60_out, b2, not_61_out);
  and and_30 (and_30_out, b6, not_62_out, b3, b2, b1);
  and and_31 (and_31_out, b6, b4, b3, not_63_out, not_64_out);
  and and_32 (and_32_out, b6, b5, b1);
  and and_33 (and_33_out, not_65_out, not_66_out, not_67_out, not_68_out, b2);
  and and_34 (and_34_out, not_69_out, not_70_out, b3, b2, b1);
  and and_35 (and_35_out, not_71_out, not_72_out, b4, not_73_out, not_74_out);
  and and_36 (and_36_out, not_75_out, not_76_out, b4, b3, not_77_out);
  and and_37 (and_37_out, not_78_out, b4, b3, not_79_out, not_80_out);
  and and_38 (and_38_out, not_34_out, b5, not_35_out, not_36_out, not_37_out, b1);
  and and_39 (and_39_out, b5, not_81_out, b2, not_82_out);
  and and_40 (and_40_out, b5, b4, not_83_out, b2, b1);
  and and_41 (and_41_out, b6, not_84_out, not_85_out, not_86_out, not_87_out);
  and and_42 (and_42_out, b6, not_88_out, not_89_out, not_90_out, b1);
  and and_43 (and_43_out, b6, not_91_out, b3, b2, not_92_out);
  and and_44 (and_44_out, b6, b4, not_93_out, b2);
  and and_45 (and_45_out, b6, b4, b2, b1);
  and and_46 (and_46_out, not_94_out, not_95_out, not_96_out, not_97_out, b1);
  and and_47 (and_47_out, not_98_out, not_99_out, not_100_out, b2, b1);
  and and_48 (and_48_out, not_101_out, not_102_out, b3, b2, not_103_out);
  and and_49 (and_49_out, not_38_out, not_39_out, b4, not_40_out, not_41_out, not_42_out);
  and and_50 (and_50_out, not_43_out, not_44_out, b4, b3, not_45_out, b1);
  and and_51 (and_51_out, b5, not_104_out, not_105_out, not_106_out);
  and and_52 (and_52_out, b5, not_107_out, b2, not_108_out);
  and and_53 (and_53_out, b5, not_109_out, b3, b1);
  and and_54 (and_54_out, b5, b3, b2, b1);
  and and_55 (and_55_out, b5, b4, b3, not_110_out, not_111_out);
  and and_56 (and_56_out, b6, not_112_out, b3, not_113_out);
  and and_57 (and_57_out, b6, b3, b2, not_114_out);
  and and_58 (and_58_out, b6, b4, not_115_out, b1);
  or or_4 (bcd1_0, and_11_out, and_12_out, and_13_out, and_14_out, and_15_out, and_16_out, and_17_out, and_18_out, and_19_out, and_20_out, and_21_out, and_22_out);
  or or_5 (bcd0_3, and_23_out, and_24_out, and_25_out, and_26_out, and_27_out, and_28_out, and_29_out, and_30_out, and_31_out, and_32_out);
  or or_6 (bcd0_2, and_33_out, and_34_out, and_35_out, and_36_out, and_37_out, and_38_out, and_39_out, and_40_out, and_41_out, and_42_out, and_43_out, and_44_out, and_45_out);
  or or_7 (bcd0_1, and_46_out, and_47_out, and_48_out, and_49_out, and_50_out, and_51_out, and_52_out, and_53_out, and_54_out, and_55_out, and_56_out, and_57_out, and_58_out);

  assign bcd_0 = b0;

  // Notes on the sheet:
  //   23CS081
endmodule

module display0to99 (
  input  [6:0] in_1
);

  wire bcdtosevensegment_1_a, bcdtosevensegment_1_b, bcdtosevensegment_1_c, bcdtosevensegment_1_d,
       bcdtosevensegment_1_dp, bcdtosevensegment_1_e, bcdtosevensegment_1_f, bcdtosevensegment_1_g,
       bcdtosevensegment_2_a, bcdtosevensegment_2_b, bcdtosevensegment_2_c, bcdtosevensegment_2_d,
       bcdtosevensegment_2_dp, bcdtosevensegment_2_e, bcdtosevensegment_2_f, bcdtosevensegment_2_g,
       sevenbitbinarytobcd_1_bcd0_1, sevenbitbinarytobcd_1_bcd0_2, sevenbitbinarytobcd_1_bcd0_3,
       sevenbitbinarytobcd_1_bcd1_0, sevenbitbinarytobcd_1_bcd1_1, sevenbitbinarytobcd_1_bcd1_2,
       sevenbitbinarytobcd_1_bcd1_3, sevenbitbinarytobcd_1_bcd_0;

  sevenbitbinarytobcd sevenbitbinarytobcd_1 (
    .b6(in_1[6]), .b5(in_1[5]), .b4(in_1[4]), .b3(in_1[3]), .b2(in_1[2]), .b1(in_1[1]), .b0(in_1[0]),
    .bcd1_3(sevenbitbinarytobcd_1_bcd1_3), .bcd1_2(sevenbitbinarytobcd_1_bcd1_2),
    .bcd1_1(sevenbitbinarytobcd_1_bcd1_1), .bcd1_0(sevenbitbinarytobcd_1_bcd1_0),
    .bcd0_3(sevenbitbinarytobcd_1_bcd0_3), .bcd0_2(sevenbitbinarytobcd_1_bcd0_2),
    .bcd0_1(sevenbitbinarytobcd_1_bcd0_1), .bcd_0(sevenbitbinarytobcd_1_bcd_0));
  bcdtosevensegment bcdtosevensegment_1 (
    .b3(sevenbitbinarytobcd_1_bcd1_3), .b2(sevenbitbinarytobcd_1_bcd1_2), .b1(sevenbitbinarytobcd_1_bcd1_1),
    .b0(sevenbitbinarytobcd_1_bcd1_0), .a(bcdtosevensegment_1_a), .b(bcdtosevensegment_1_b),
    .c(bcdtosevensegment_1_c), .d(bcdtosevensegment_1_d), .e(bcdtosevensegment_1_e),
    .f(bcdtosevensegment_1_f), .g(bcdtosevensegment_1_g), .dp(bcdtosevensegment_1_dp));
  _7_Segment_Display u_7_segment_display_1 (
    .g(bcdtosevensegment_1_g), .f(bcdtosevensegment_1_f), .a(bcdtosevensegment_1_a),
    .b(bcdtosevensegment_1_b), .e(bcdtosevensegment_1_e), .d(bcdtosevensegment_1_d),
    .c(bcdtosevensegment_1_c), .dp(bcdtosevensegment_1_dp));
  bcdtosevensegment bcdtosevensegment_2 (
    .b3(sevenbitbinarytobcd_1_bcd0_3), .b2(sevenbitbinarytobcd_1_bcd0_2), .b1(sevenbitbinarytobcd_1_bcd0_1),
    .b0(sevenbitbinarytobcd_1_bcd_0), .a(bcdtosevensegment_2_a), .b(bcdtosevensegment_2_b),
    .c(bcdtosevensegment_2_c), .d(bcdtosevensegment_2_d), .e(bcdtosevensegment_2_e),
    .f(bcdtosevensegment_2_f), .g(bcdtosevensegment_2_g), .dp(bcdtosevensegment_2_dp));
  _7_Segment_Display u_7_segment_display_2 (
    .g(bcdtosevensegment_2_g), .f(bcdtosevensegment_2_f), .a(bcdtosevensegment_2_a),
    .b(bcdtosevensegment_2_b), .e(bcdtosevensegment_2_e), .d(bcdtosevensegment_2_d),
    .c(bcdtosevensegment_2_c), .dp(bcdtosevensegment_2_dp));

  // Notes on the sheet:
  //   23CS081
endmodule
