// Logisim project exp2.circ as structural Verilog: 1 circuit, main circuit main
module main (
  input  As,
  input  Bs,
  input  M,
  input  [6:0] A,
  input  [6:0] B,
  input  [6:0] zeroes,
  input  [6:0] zeroes_2,
  output signs,
  output Calling_Control,
  output [6:0] Result_A,
  output E,
  output [6:0] out_12,
  output [6:0] Final_A,
  output Final__As,
  output AVF
);

  wire comparator_1_eq, multiplexer_2_out, multiplexer_6_out, not_3_out;
  wire [6:0] adder_2_out, multiplexer_4_out, not_1_out, not_2_out;

  assign not_1_out = ~B;  // NOT_Gate not_1, 7 bits wide
  xor xor_1 (signs, As, Bs);
  Multiplexer #(.width(7), .enable("false")) multiplexer_1 (
    .in0(B), .in1(not_1_out), .out(out_12), .sel(Calling_Control));
  Comparator #(.width(7)) comparator_1 (.a(Result_A), .b(zeroes_2), .eq(comparator_1_eq));  // open: gt, lt
  Adder #(.width(7)) adder_1 (.a(A), .b(out_12), .out(Result_A), .cin(Calling_Control), .cout(E));
  Multiplexer #(.enable("false")) multiplexer_2 (.in0(As), .in1(1'b0), .out(multiplexer_2_out), .sel(comparator_1_eq));
  xor xor_2 (Calling_Control, signs, M);
  assign not_2_out = ~Result_A;  // NOT_Gate not_2, 7 bits wide
  not not_3 (not_3_out, As);
  Multiplexer #(.width(7), .enable("false")) multiplexer_3 (
    .in0(Result_A), .in1(multiplexer_4_out), .out(Final_A), .sel(Calling_Control));
  Multiplexer #(.width(7), .enable("false")) multiplexer_4 (
    .in0(adder_2_out), .in1(Result_A), .out(multiplexer_4_out), .sel(E));
  Multiplexer #(.enable("false")) multiplexer_5 (
    .in0(As), .in1(multiplexer_6_out), .out(Final__As), .sel(Calling_Control));
  Multiplexer #(.enable("false")) multiplexer_6 (
    .in0(not_3_out), .in1(multiplexer_2_out), .out(multiplexer_6_out), .sel(E));
  Multiplexer #(.enable("false")) multiplexer_7 (.in0(E), .in1(1'b0), .out(AVF), .sel(Calling_Control));
  Adder #(.width(7)) adder_2 (.a(not_2_out), .b(zeroes), .out(adder_2_out), .cin(Calling_Control));  // open: cout

  // Notes on the sheet:
  //   Sign bit of number A
  //   Sign bit of number B
  //   magnitude of number A
  //   magnitude of number B
  //   if signs=0: both number have same signs 
  //   if signs=1: both number have diff. signs 
  //   M=0: Addition
  //   M=1: Subtraction
  //   calling control=0, then call fun. 1: add magnitude of both num. and use sign of num A
  //   Result A
  //   calling control=1. then call fun. 2  subtract smaller num from larger num. and use sign of larger num.
  //   As
  //   E
endmodule
