// Logisim project exp_3.circ as structural Verilog: 2 circuits, main circuit main
module main (
  input  [1:0] _00__Register_d,
  input  [3:0] Input_For_Register_D,
  input  [3:0] Input_for_Register_A,
  input  [3:0] Input_for_Register_C,
  input  [3:0] Input_for_Register_B,
  output [3:0] Common_bus,
  output [3:0] out_7,
  output [3:0] out_8,
  output [3:0] out_9,
  output [3:0] out_10
);

  wire clock_1_out;

  Clock clock_1 (.out(clock_1_out));
  Multiplexer #(.select(2), .enable("false")) multiplexer_1 (
    .in0(out_7[3]), .in1(out_8[3]), .in2(out_10[3]), .in3(out_9[3]), .out(Common_bus[3]),
    .sel(_00__Register_d));
  Register #(.width(4)) Register_D (.D(Input_For_Register_D), .en(1'b1), .Q(out_7), .clk(clock_1_out), .clr(1'b0));
  Multiplexer #(.select(2), .enable("false")) multiplexer_2 (
    .in0(out_7[2]), .in1(out_8[2]), .in2(out_10[2]), .in3(out_9[2]), .out(Common_bus[2]),
    .sel(_00__Register_d));
  Register #(.width(4)) Register_C (.D(Input_for_Register_C), .en(1'b1), .Q(out_8), .clk(clock_1_out), .clr(1'b0));
  Multiplexer #(.select(2), .enable("false")) multiplexer_3 (
    .in0(out_7[1]), .in1(out_8[1]), .in2(out_10[1]), .in3(out_9[1]), .out(Common_bus[1]),
    .sel(_00__Register_d));
  Register #(.width(4)) Register_B (.D(Input_for_Register_B), .en(1'b1), .Q(out_10), .clk(clock_1_out), .clr(1'b0));
  Multiplexer #(.select(2), .enable("false")) multiplexer_4 (
    .in0(out_7[0]), .in1(out_8[0]), .in2(out_10[0]), .in3(out_9[0]), .out(Common_bus[0]),
    .sel(_00__Register_d));
  Register #(.width(4)) Register_A (.D(Input_for_Register_A), .en(1'b1), .Q(out_9), .clk(clock_1_out), .clr(1'b0));

  // Notes on the sheet:
  //   01: Register C
  //   10: Register B
  //   11: Register A
  //   Bit 3
  //   D3
  //   A3
  //   23CS081
  //   D2
  //   Bit 2
  //   A2
  //   D1
  //   Bit 1
  //   A1
  //   Bit 0
  //   A0
  //   D0
endmodule

module CK2_2 (
  input  [1:0] S1_S0,
  input  [3:0] Input_For_Register_D,
  input  [3:0] Input_for_Register_A,
  input  [3:0] Input_for_Register_C,
  input  [3:0] Input_for_Register_B,
  output [3:0] Common_bus,
  output [3:0] out_7,
  output [3:0] out_8,
  output [3:0] out_9,
  output [3:0] out_10
);

  wire clock_1_out, decoder_1_out0, decoder_1_out1, decoder_1_out2, decoder_1_out3;

  Decoder #(.select(2), .enable("false")) decoder_1 (
    .out0(decoder_1_out0), .out1(decoder_1_out1), .out2(decoder_1_out2), .out3(decoder_1_out3), .sel(S1_S0));
  Clock clock_1 (.out(clock_1_out));
  Register #(.width(4)) Register_D (.D(Input_For_Register_D), .en(1'b1), .Q(out_7), .clk(clock_1_out), .clr(1'b0));
  assign Common_bus[3] = decoder_1_out0 ? out_9[3] : 1'bz;  // Controlled_Buffer controlled_buffer_1
  assign Common_bus[3] = decoder_1_out1 ? out_10[3] : 1'bz;  // Controlled_Buffer controlled_buffer_2
  assign Common_bus[3] = decoder_1_out2 ? out_8[3] : 1'bz;  // Controlled_Buffer controlled_buffer_3
  assign Common_bus[3] = decoder_1_out3 ? out_7[3] : 1'bz;  // Controlled_Buffer controlled_buffer_4
  assign Common_bus[2] = decoder_1_out0 ? out_9[2] : 1'bz;  // Controlled_Buffer controlled_buffer_5
  assign Common_bus[2] = decoder_1_out1 ? out_10[2] : 1'bz;  // Controlled_Buffer controlled_buffer_6
  assign Common_bus[2] = decoder_1_out2 ? out_8[2] : 1'bz;  // Controlled_Buffer controlled_buffer_7
  assign Common_bus[2] = decoder_1_out3 ? out_7[2] : 1'bz;  // Controlled_Buffer controlled_buffer_8
  Register #(.width(4)) Register_C (.D(Input_for_Register_C), .en(1'b1), .Q(out_8), .clk(clock_1_out), .clr(1'b0));
  assign Common_bus[1] = decoder_1_out0 ? out_9[1] : 1'bz;  // Controlled_Buffer controlled_buffer_9
  assign Common_bus[1] = decoder_1_out1 ? out_10[1] : 1'bz;  // Controlled_Buffer controlled_buffer_10
  assign Common_bus[1] = decoder_1_out2 ? out_8[1] : 1'bz;  // Controlled_Buffer controlled_buffer_11
  assign Common_bus[1] = decoder_1_out3 ? out_7[1] : 1'bz;  // Controlled_Buffer controlled_buffer_12
  Register #(.width(4)) Register_B (.D(Input_for_Register_B), .en(1'b1), .Q(out_10), .clk(clock_1_out), .clr(1'b0));
  assign Common_bus[0] = decoder_1_out0 ? out_9[0] : 1'bz;  // Controlled_Buffer controlled_buffer_13
  assign Common_bus[0] = decoder_1_out1 ? out_10[0] : 1'bz;  // Controlled_Buffer controlled_buffer_14
  assign Common_bus[0] = decoder_1_out2 ? out_8[0] : 1'bz;  // Controlled_Buffer controlled_buffer_15
  assign Common_bus[0] = decoder_1_out3 ? out_7[0] : 1'bz;  // Controlled_Buffer controlled_buffer_16
  Register #(.width(4)) Register_A (.D(Input_for_Register_A), .en(1'b1), .Q(out_9), .clk(clock_1_out), .clr(1'b0));

  // Notes on the sheet:
  //   A3
  //   B3
  //   C3
  //   D3
  //   23CS081
  //   A2
  //   B2
  //   C2
  //   D2
  //   A1
  //   B1
  //   C1
  //   D1
  //   A0
  //   B0
  //   C0
  //   D0
endmodule
