// Logisim project exp_3_my.circ as structural Verilog: 2 circuits, main circuit main
module main (
  input  [1:0] _00__Register_C,
  input  [3:0] Input_for_Register_C,
  input  [3:0] Input_for_Register_B,
  input  [3:0] Input_for_Register_A,
  output [3:0] Common_bus,
  output [3:0] out_6,
  output [3:0] out_7,
  output [3:0] out_8
);

  wire clock_1_out;

  Multiplexer #(.select(2), .enable("false")) multiplexer_1 (
    .in0(out_6[3]), .in1(out_7[3]), .in2(out_8[3]), .in3(out_8[3]), .out(Common_bus[3]), .sel(_00__Register_C));
  Clock clock_1 (.out(clock_1_out));
  Register #(.width(4)) Register_C (.D(Input_for_Register_C), .en(1'b1), .Q(out_6), .clk(clock_1_out), .clr(1'b0));
  Multiplexer #(.select(2), .enable("false")) multiplexer_2 (
    .in0(out_6[2]), .in1(out_7[2]), .in2(out_8[2]), .in3(out_8[2]), .out(Common_bus[2]), .sel(_00__Register_C));
  Multiplexer #(.select(2), .enable("false")) multiplexer_3 (
    .in0(out_6[1]), .in1(out_7[1]), .in2(out_8[1]), .in3(out_8[1]), .out(Common_bus[1]), .sel(_00__Register_C));
  Register #(.width(4)) Register_B (.D(Input_for_Register_B), .en(1'b1), .Q(out_7), .clk(clock_1_out), .clr(1'b0));
  Multiplexer #(.select(2), .enable("false")) multiplexer_4 (
    .in0(out_6[0]), .in1(out_7[0]), .in2(out_8[0]), .in3(out_8[0]), .out(Common_bus[0]), .sel(_00__Register_C));
  Register #(.width(4)) Register_A (.D(Input_for_Register_A), .en(1'b1), .Q(out_8), .clk(clock_1_out), .clr(1'b0));

  // Notes on the sheet:
  //   01: Register B
  //   11 & 10: Register A
  //   23CS081
endmodule

module ckt_2 (
  input  [1:0] in_1,
  input  [3:0] Input_for_Register_C,
  input  [3:0] Input_for_Register_B,
  input  [3:0] Input_for_Register_A,
  output [3:0] Common_bus,
  output [3:0] out_6,
  output [3:0] out_7,
  output [3:0] out_8
);

  wire clock_1_out, decoder_1_out0, decoder_1_out1, decoder_1_out2, decoder_1_out3, or_1_out;

  Decoder #(.select(2), .enable("false")) decoder_1 (
    .out0(decoder_1_out0), .out1(decoder_1_out1), .out2(decoder_1_out2), .out3(decoder_1_out3), .sel(in_1));
  or or_1 (or_1_out, decoder_1_out2, decoder_1_out3);
  Register #(.width(4)) Register_C (.D(Input_for_Register_C), .en(1'b1), .Q(out_6), .clk(clock_1_out), .clr(1'b0));
  Clock clock_1 (.out(clock_1_out));
  assign Common_bus[3] = decoder_1_out0 ? out_8[3] : 1'bz;  // Controlled_Buffer controlled_buffer_1
  assign Common_bus[3] = decoder_1_out1 ? out_7[3] : 1'bz;  // Controlled_Buffer controlled_buffer_2
  assign Common_bus[3] = or_1_out ? out_6[3] : 1'bz;  // Controlled_Buffer controlled_buffer_3
  assign Common_bus[2] = decoder_1_out0 ? out_8[2] : 1'bz;  // Controlled_Buffer controlled_buffer_4
  assign Common_bus[2] = decoder_1_out1 ? out_7[2] : 1'bz;  // Controlled_Buffer controlled_buffer_5
  assign Common_bus[2] = or_1_out ? out_6[2] : 1'bz;  // Controlled_Buffer controlled_buffer_6
  assign Common_bus[1] = decoder_1_out0 ? out_8[1] : 1'bz;  // Controlled_Buffer controlled_buffer_7
  assign Common_bus[1] = decoder_1_out1 ? out_7[1] : 1'bz;  // Controlled_Buffer controlled_buffer_8
  assign Common_bus[1] = or_1_out ? out_6[1] : 1'bz;  // Controlled_Buffer controlled_buffer_9
  Register #(.width(4)) Register_B (.D(Input_for_Register_B), .en(1'b1), .Q(out_7), .clk(clock_1_out), .clr(1'b0));
  assign Common_bus[0] = decoder_1_out0 ? out_8[0] : 1'bz;  // Controlled_Buffer controlled_buffer_10
  assign Common_bus[0] = decoder_1_out1 ? out_7[0] : 1'bz;  // Controlled_Buffer controlled_buffer_11
  assign Common_bus[0] = or_1_out ? out_6[0] : 1'bz;  // Controlled_Buffer controlled_buffer_12
  Register #(.width(4)) Register_A (.D(Input_for_Register_A), .en(1'b1), .Q(out_8), .clk(clock_1_out), .clr(1'b0));

  // Notes on the sheet:
  //   A3
  //   B3
  //   C3
  //   A2
  //   B2
  //   C2
  //   A1
  //   B1
  //   C1
  //   A0
  //   B0
  //   C0
endmodule
