// Logisim project exp_4.circ as structural Verilog
module one_bit_arithmetic (
  input  Cin,
  input  A0,
  input  B0,
  input  [1:0] S1S0,
  output D0,
  output Cout
);

  wire multiplexer_1_out, not_1_out, not_2_out, xor_1_out;

  not not_1 (not_1_out, B0);
  not not_2 (not_2_out, xor_1_out);
  xor xor_1 (xor_1_out, B0, B0);
  Multiplexer #(.select(2), .enable("false")) multiplexer_1 (
    .in0(B0), .in1(not_1_out), .in2(xor_1_out), .in3(not_2_out), .out(multiplexer_1_out), .sel(S1S0));
  Adder #(.width(1)) adder_1 (.a(A0), .b(multiplexer_1_out), .out(D0), .cin(Cin), .cout(Cout));

  // Notes on the sheet:
  //   23CS081
endmodule

module two_bit_arithmetic (
  input  [1:0] A1A0,
  input  [1:0] b1b0,
  input  Cin,
  input  [1:0] in_4,
  output [1:0] D1D0,
  output Cout
);

  wire adder_1_cout, multiplexer_1_out, multiplexer_2_out, not_1_out, not_2_out, not_3_out, not_4_out,
       xor_1_out, xor_2_out;

  not not_1 (not_1_out, b1b0[0]);
  xor xor_1 (xor_1_out, b1b0[0], b1b0[0]);
  not not_2 (not_2_out, b1b0[1]);
  xor xor_2 (xor_2_out, b1b0[1], b1b0[1]);
  Multiplexer #(.select(2), .enable("false")) multiplexer_1 (
    .in0(b1b0[0]), .in1(not_1_out), .in2(xor_1_out), .in3(not_3_out), .out(multiplexer_1_out), .sel(in_4));
  not not_3 (not_3_out, xor_1_out);
  Multiplexer #(.select(2), .enable("false")) multiplexer_2 (
    .in0(b1b0[1]), .in1(not_2_out), .in2(xor_2_out), .in3(not_4_out), .out(multiplexer_2_out), .sel(in_4));
  not not_4 (not_4_out, xor_2_out);
  Adder #(.width(1)) adder_1 (.a(A1A0[0]), .b(multiplexer_1_out), .out(D1D0[1]), .cin(Cin), .cout(adder_1_cout));
  Adder #(.width(1)) adder_2 (.a(A1A0[1]), .b(multiplexer_2_out), .out(D1D0[0]), .cin(adder_1_cout), .cout(Cout));

  // Notes on the sheet:
  //   23CS081
endmodule

module four_bit_arithmetic (
  input  [1:0] S1S0,
  input  Cin,
  input  [3:0] A3A2A1A0,
  input  [3:0] B3B2B1B0,
  output [3:0] D3D2D1D0,
  output Cout
);

  wire adder_1_cout, adder_2_cout, adder_3_cout, multiplexer_1_out, multiplexer_2_out, multiplexer_3_out,
       multiplexer_4_out, not_1_out, not_2_out, not_3_out, not_4_out, not_5_out, not_6_out, not_7_out,
       not_8_out, xor_1_out, xor_2_out, xor_3_out, xor_4_out;

  not not_1 (not_1_out, B3B2B1B0[0]);
  xor xor_1 (xor_1_out, B3B2B1B0[0], B3B2B1B0[0]);
  not not_2 (not_2_out, xor_1_out);
  not not_3 (not_3_out, B3B2B1B0[1]);
  xor xor_2 (xor_2_out, B3B2B1B0[1], B3B2B1B0[1]);
  not not_4 (not_4_out, B3B2B1B0[2]);
  xor xor_3 (xor_3_out, B3B2B1B0[2], B3B2B1B0[2]);
  not not_5 (not_5_out, xor_3_out);
  not not_6 (not_6_out, B3B2B1B0[3]);
  xor xor_4 (xor_4_out, B3B2B1B0[3], B3B2B1B0[3]);
  Multiplexer #(.select(2), .enable("false")) multiplexer_1 (
    .in0(B3B2B1B0[0]), .in1(not_1_out), .in2(xor_1_out), .in3(not_2_out), .out(multiplexer_1_out), .sel(S1S0));
  Multiplexer #(.select(2), .enable("false")) multiplexer_2 (
    .in0(B3B2B1B0[1]), .in1(not_3_out), .in2(xor_2_out), .in3(not_7_out), .out(multiplexer_2_out), .sel(S1S0));
  not not_7 (not_7_out, xor_2_out);
  Multiplexer #(.select(2), .enable("false")) multiplexer_3 (
    .in0(B3B2B1B0[2]), .in1(not_4_out), .in2(xor_3_out), .in3(not_5_out), .out(multiplexer_3_out), .sel(S1S0));
  Multiplexer #(.select(2), .enable("false")) multiplexer_4 (
    .in0(B3B2B1B0[3]), .in1(not_6_out), .in2(xor_4_out), .in3(not_8_out), .out(multiplexer_4_out), .sel(S1S0));
  not not_8 (not_8_out, xor_4_out);
  Adder #(.width(1)) adder_1 (
    .a(A3A2A1A0[0]), .b(multiplexer_1_out), .out(D3D2D1D0[0]), .cin(Cin), .cout(adder_1_cout));
  Adder #(.width(1)) adder_2 (
    .a(A3A2A1A0[1]), .b(multiplexer_2_out), .out(D3D2D1D0[1]), .cin(adder_1_cout), .cout(adder_2_cout));
  Adder #(.width(1)) adder_3 (
    .a(A3A2A1A0[2]), .b(multiplexer_3_out), .out(D3D2D1D0[2]), .cin(adder_2_cout), .cout(adder_3_cout));
  Adder #(.width(1)) adder_4 (
    .a(A3A2A1A0[3]), .b(multiplexer_4_out), .out(D3D2D1D0[3]), .cin(adder_3_cout), .cout(Cout));

  // Notes on the sheet:
  //   23CS081
endmodule

module eight_bit_arithmetic (
  input  [1:0] S1S0,
  input  [7:0] A7A6A5A4A3A2A1A0,
  input  [7:0] B7B6B5B4B3B2B1B0,
  input  Cin,
  output Cout,
  output [7:0] D7D6D5D4D3D2D1D0
);

  wire adder_1_cout, adder_2_cout, adder_3_cout, adder_4_cout, adder_5_cout, adder_6_cout, adder_7_cout,
       multiplexer_1_out, multiplexer_2_out, multiplexer_3_out, multiplexer_4_out, multiplexer_5_out,
       multiplexer_6_out, multiplexer_7_out, multiplexer_8_out, not_1_out, not_2_out, not_3_out, not_4_out,
       not_5_out, not_6_out, not_7_out, not_8_out, not_9_out, not_10_out, not_11_out, not_12_out, not_13_out,
       not_14_out, not_15_out, not_16_out, xor_1_out, xor_2_out, xor_3_out, xor_4_out, xor_5_out, xor_6_out,
       xor_7_out, xor_8_out;

  not not_1 (not_1_out, B7B6B5B4B3B2B1B0[0]);
  not not_2 (not_2_out, xor_1_out);
  xor xor_1 (xor_1_out, B7B6B5B4B3B2B1B0[0], B7B6B5B4B3B2B1B0[0]);
  not not_3 (not_3_out, B7B6B5B4B3B2B1B0[1]);
  xor xor_2 (xor_2_out, B7B6B5B4B3B2B1B0[1], B7B6B5B4B3B2B1B0[1]);
  not not_4 (not_4_out, B7B6B5B4B3B2B1B0[2]);
  xor xor_3 (xor_3_out, B7B6B5B4B3B2B1B0[2], B7B6B5B4B3B2B1B0[2]);
  not not_5 (not_5_out, xor_3_out);
  not not_6 (not_6_out, B7B6B5B4B3B2B1B0[3]);
  xor xor_4 (xor_4_out, B7B6B5B4B3B2B1B0[3], B7B6B5B4B3B2B1B0[3]);
  Multiplexer #(.select(2), .enable("false")) multiplexer_1 (
    .in0(B7B6B5B4B3B2B1B0[0]), .in1(not_1_out), .in2(xor_1_out), .in3(not_2_out), .out(multiplexer_1_out),
    .sel(S1S0));
  Multiplexer #(.select(2), .enable("false")) multiplexer_2 (
    .in0(B7B6B5B4B3B2B1B0[1]), .in1(not_3_out), .in2(xor_2_out), .in3(not_7_out), .out(multiplexer_2_out),
    .sel(S1S0));
  not not_7 (not_7_out, xor_2_out);
  Multiplexer #(.select(2), .enable("false")) multiplexer_3 (
    .in0(B7B6B5B4B3B2B1B0[2]), .in1(not_4_out), .in2(xor_3_out), .in3(not_5_out), .out(multiplexer_3_out),
    .sel(S1S0));
  Multiplexer #(.select(2), .enable("false")) multiplexer_4 (
    .in0(B7B6B5B4B3B2B1B0[3]), .in1(not_6_out), .in2(xor_4_out), .in3(not_8_out), .out(multiplexer_4_out),
    .sel(S1S0));
  not not_8 (not_8_out, xor_4_out);
  Adder #(.width(1)) adder_1 (
    .a(A7A6A5A4A3A2A1A0[0]), .b(multiplexer_1_out), .out(D7D6D5D4D3D2D1D0[0]), .cin(Cin), .cout(adder_1_cout));
  Adder #(.width(1)) adder_2 (
    .a(A7A6A5A4A3A2A1A0[1]), .b(multiplexer_2_out), .out(D7D6D5D4D3D2D1D0[1]), .cin(adder_1_cout),
    .cout(adder_2_cout));
  Adder #(.width(1)) adder_3 (
    .a(A7A6A5A4A3A2A1A0[2]), .b(multiplexer_3_out), .out(D7D6D5D4D3D2D1D0[2]), .cin(adder_2_cout),
    .cout(adder_3_cout));
  Adder #(.width(1)) adder_4 (
    .a(A7A6A5A4A3A2A1A0[3]), .b(multiplexer_4_out), .out(D7D6D5D4D3D2D1D0[3]), .cin(adder_3_cout),
    .cout(adder_4_cout));
  not not_9 (not_9_out, B7B6B5B4B3B2B1B0[4]);
  xor xor_5 (xor_5_out, B7B6B5B4B3B2B1B0[4], B7B6B5B4B3B2B1B0[4]);
  not not_10 (not_10_out, B7B6B5B4B3B2B1B0[5]);
  xor xor_6 (xor_6_out, B7B6B5B4B3B2B1B0[5], B7B6B5B4B3B2B1B0[5]);
  not not_11 (not_11_out, B7B6B5B4B3B2B1B0[6]);
  xor xor_7 (xor_7_out, B7B6B5B4B3B2B1B0[6], B7B6B5B4B3B2B1B0[6]);
  not not_12 (not_12_out, B7B6B5B4B3B2B1B0[7]);
  xor xor_8 (xor_8_out, B7B6B5B4B3B2B1B0[7], B7B6B5B4B3B2B1B0[7]);
  Multiplexer #(.select(2), .enable("false")) multiplexer_5 (
    .in0(B7B6B5B4B3B2B1B0[4]), .in1(not_9_out), .in2(xor_5_out), .in3(not_13_out), .out(multiplexer_5_out),
    .sel(S1S0));
  not not_13 (not_13_out, xor_5_out);
  not not_14 (not_14_out, xor_6_out);
  Multiplexer #(.select(2), .enable("false")) multiplexer_6 (
    .in0(B7B6B5B4B3B2B1B0[6]), .in1(not_11_out), .in2(xor_7_out), .in3(not_15_out), .out(multiplexer_6_out),
    .sel(S1S0));
  not not_15 (not_15_out, xor_7_out);
  not not_16 (not_16_out, xor_8_out);
  Multiplexer #(.select(2), .enable("false")) multiplexer_7 (
    .in0(B7B6B5B4B3B2B1B0[5]), .in1(not_10_out), .in2(xor_6_out), .in3(not_14_out), .out(multiplexer_7_out),
    .sel(S1S0));
  Multiplexer #(.select(2), .enable("false")) multiplexer_8 (
    .in0(B7B6B5B4B3B2B1B0[7]), .in1(not_12_out), .in2(xor_8_out), .in3(not_16_out), .out(multiplexer_8_out),
    .sel(S1S0));
  Adder #(.width(1)) adder_5 (
    .a(A7A6A5A4A3A2A1A0[4]), .b(multiplexer_5_out), .out(D7D6D5D4D3D2D1D0[4]), .cin(adder_4_cout),
    .cout(adder_5_cout));
  Adder #(.width(1)) adder_6 (
    .a(A7A6A5A4A3A2A1A0[5]), .b(multiplexer_7_out), .out(D7D6D5D4D3D2D1D0[5]), .cin(adder_5_cout),
    .cout(adder_6_cout));
  Adder #(.width(1)) adder_7 (
    .a(A7A6A5A4A3A2A1A0[6]), .b(multiplexer_6_out), .out(D7D6D5D4D3D2D1D0[6]), .cin(adder_6_cout),
    .cout(adder_7_cout));
  Adder #(.width(1)) adder_8 (
    .a(A7A6A5A4A3A2A1A0[7]), .b(multiplexer_8_out), .out(D7D6D5D4D3D2D1D0[7]), .cin(adder_7_cout), .cout(Cout));

  // Notes on the sheet:
  //   23CS081
endmodule

module one_bit_logical (
  input  [1:0] S1S0,
  input  B0,
  input  A0,
  output E0
);

  wire and_1_out, not_1_out, or_1_out, xor_1_out;

  and and_1 (and_1_out, A0, B0);
  or or_1 (or_1_out, A0, B0);
  xor xor_1 (xor_1_out, A0, B0);
  not not_1 (not_1_out, A0);
  Multiplexer #(.select(2), .enable("false")) multiplexer_1 (
    .in0(and_1_out), .in1(or_1_out), .in2(xor_1_out), .in3(not_1_out), .out(E0), .sel(S1S0));

  // Notes on the sheet:
  //   23CS081
endmodule

module two_bit_logical (
  input  [1:0] B1B0,
  input  [1:0] A1A0,
  input  [1:0] S1S0,
  output [1:0] E1E0
);

  wire and_1_out, and_2_out, not_1_out, not_2_out, or_1_out, or_2_out, xor_1_out, xor_2_out;

  and and_1 (and_1_out, A1A0[0], B1B0[0]);
  or or_1 (or_1_out, A1A0[0], B1B0[0]);
  xor xor_1 (xor_1_out, A1A0[0], B1B0[0]);
  not not_1 (not_1_out, A1A0[0]);
  and and_2 (and_2_out, A1A0[1], B1B0[1]);
  or or_2 (or_2_out, A1A0[1], B1B0[1]);
  xor xor_2 (xor_2_out, A1A0[1], B1B0[1]);
  not not_2 (not_2_out, A1A0[1]);
  Multiplexer #(.select(2), .enable("false")) multiplexer_1 (
    .in0(and_1_out), .in1(or_1_out), .in2(xor_1_out), .in3(not_1_out), .out(E1E0[0]), .sel(S1S0));
  Multiplexer #(.select(2), .enable("false")) multiplexer_2 (
    .in0(and_2_out), .in1(or_2_out), .in2(xor_2_out), .in3(not_2_out), .out(E1E0[1]), .sel(S1S0));

  // Notes on the sheet:
  //   23CS081
endmodule

module four_bit_logical (
  input  [1:0] S1S0,
  input  [3:0] B3B2B1B0,
  input  [3:0] A3A2A1A0,
  output [3:0] E3E2E1E0
);

  wire and_1_out, and_2_out, and_3_out, and_4_out, not_1_out, not_2_out, not_3_out, not_4_out, or_1_out,
       or_2_out, or_3_out, or_4_out, xor_1_out, xor_2_out, xor_3_out, xor_4_out;

  and and_1 (and_1_out, A3A2A1A0[0], B3B2B1B0[0]);
  or or_1 (or_1_out, A3A2A1A0[0], B3B2B1B0[0]);
  xor xor_1 (xor_1_out, A3A2A1A0[0], B3B2B1B0[0]);
  not not_1 (not_1_out, A3A2A1A0[0]);
  and and_2 (and_2_out, A3A2A1A0[1], B3B2B1B0[1]);
  or or_2 (or_2_out, A3A2A1A0[1], B3B2B1B0[1]);
  xor xor_2 (xor_2_out, A3A2A1A0[1], B3B2B1B0[1]);
  not not_2 (not_2_out, A3A2A1A0[1]);
  and and_3 (and_3_out, A3A2A1A0[2], B3B2B1B0[2]);
  or or_3 (or_3_out, A3A2A1A0[2], B3B2B1B0[2]);
  xor xor_3 (xor_3_out, A3A2A1A0[2], B3B2B1B0[2]);
  not not_3 (not_3_out, A3A2A1A0[2]);
  and and_4 (and_4_out, A3A2A1A0[3], B3B2B1B0[3]);
  or or_4 (or_4_out, A3A2A1A0[3], B3B2B1B0[3]);
  xor xor_4 (xor_4_out, A3A2A1A0[3], B3B2B1B0[3]);
  not not_4 (not_4_out, A3A2A1A0[3]);
  Multiplexer #(.select(2), .enable("false")) multiplexer_1 (
    .in0(and_1_out), .in1(or_1_out), .in2(xor_1_out), .in3(not_1_out), .out(E3E2E1E0[0]), .sel(S1S0));
  Multiplexer #(.select(2), .enable("false")) multiplexer_2 (
    .in0(and_2_out), .in1(or_2_out), .in2(xor_2_out), .in3(not_2_out), .out(E3E2E1E0[1]), .sel(S1S0));
  Multiplexer #(.select(2), .enable("false")) multiplexer_3 (
    .in0(and_3_out), .in1(or_3_out), .in2(xor_3_out), .in3(not_3_out), .out(E3E2E1E0[2]), .sel(S1S0));
  Multiplexer #(.select(2), .enable("false")) multiplexer_4 (
    .in0(and_4_out), .in1(or_4_out), .in2(xor_4_out), .in3(not_4_out), .out(E3E2E1E0[3]), .sel(S1S0));

  // Notes on the sheet:
  //   23CS081
endmodule

module eight_bit_logical (
  input  [1:0] S1S0,
  input  [7:0] B7B6B5B4B3B2B1B0,
  input  [7:0] A7A6A5A4A3A2A1A0,
  output [7:0] E7E6E5E4E3E2E1E0
);

  wire and_1_out, and_2_out, and_3_out, and_4_out, and_5_out, and_6_out, and_7_out, and_8_out, not_1_out,
       not_2_out, not_3_out, not_4_out, not_5_out, not_6_out, not_7_out, not_8_out, or_1_out, or_2_out,
       or_3_out, or_4_out, or_5_out, or_6_out, or_7_out, or_8_out, xor_1_out, xor_2_out, xor_3_out,
       xor_4_out, xor_5_out, xor_6_out, xor_7_out, xor_8_out;

  and and_1 (and_1_out, A7A6A5A4A3A2A1A0[0], B7B6B5B4B3B2B1B0[0]);
  or or_1 (or_1_out, A7A6A5A4A3A2A1A0[0], B7B6B5B4B3B2B1B0[0]);
  xor xor_1 (xor_1_out, A7A6A5A4A3A2A1A0[0], B7B6B5B4B3B2B1B0[0]);
  not not_1 (not_1_out, A7A6A5A4A3A2A1A0[0]);
  and and_2 (and_2_out, A7A6A5A4A3A2A1A0[1], B7B6B5B4B3B2B1B0[1]);
  or or_2 (or_2_out, A7A6A5A4A3A2A1A0[1], B7B6B5B4B3B2B1B0[1]);
  xor xor_2 (xor_2_out, A7A6A5A4A3A2A1A0[1], B7B6B5B4B3B2B1B0[1]);
  not not_2 (not_2_out, A7A6A5A4A3A2A1A0[1]);
  and and_3 (and_3_out, A7A6A5A4A3A2A1A0[2], B7B6B5B4B3B2B1B0[2]);
  or or_3 (or_3_out, A7A6A5A4A3A2A1A0[2], B7B6B5B4B3B2B1B0[2]);
  xor xor_3 (xor_3_out, A7A6A5A4A3A2A1A0[2], B7B6B5B4B3B2B1B0[2]);
  not not_3 (not_3_out, A7A6A5A4A3A2A1A0[2]);
  and and_4 (and_4_out, A7A6A5A4A3A2A1A0[3], B7B6B5B4B3B2B1B0[3]);
  or or_4 (or_4_out, A7A6A5A4A3A2A1A0[3], B7B6B5B4B3B2B1B0[3]);
  xor xor_4 (xor_4_out, A7A6A5A4A3A2A1A0[3], B7B6B5B4B3B2B1B0[3]);
  not not_4 (not_4_out, A7A6A5A4A3A2A1A0[3]);
  and and_5 (and_5_out, A7A6A5A4A3A2A1A0[4], B7B6B5B4B3B2B1B0[4]);
  or or_5 (or_5_out, A7A6A5A4A3A2A1A0[4], B7B6B5B4B3B2B1B0[4]);
  xor xor_5 (xor_5_out, A7A6A5A4A3A2A1A0[4], B7B6B5B4B3B2B1B0[4]);
  not not_5 (not_5_out, A7A6A5A4A3A2A1A0[4]);
  and and_6 (and_6_out, A7A6A5A4A3A2A1A0[5], B7B6B5B4B3B2B1B0[5]);
  or or_6 (or_6_out, A7A6A5A4A3A2A1A0[5], B7B6B5B4B3B2B1B0[5]);
  xor xor_6 (xor_6_out, A7A6A5A4A3A2A1A0[5], B7B6B5B4B3B2B1B0[5]);
  not not_6 (not_6_out, A7A6A5A4A3A2A1A0[5]);
  and and_7 (and_7_out, A7A6A5A4A3A2A1A0[6], B7B6B5B4B3B2B1B0[6]);
  or or_7 (or_7_out, A7A6A5A4A3A2A1A0[6], B7B6B5B4B3B2B1B0[6]);
  xor xor_7 (xor_7_out, A7A6A5A4A3A2A1A0[6], B7B6B5B4B3B2B1B0[6]);
  not not_7 (not_7_out, A7A6A5A4A3A2A1A0[6]);
  and and_8 (and_8_out, A7A6A5A4A3A2A1A0[7], B7B6B5B4B3B2B1B0[7]);
  or or_8 (or_8_out, A7A6A5A4A3A2A1A0[7], B7B6B5B4B3B2B1B0[7]);
  xor xor_8 (xor_8_out, A7A6A5A4A3A2A1A0[7], B7B6B5B4B3B2B1B0[7]);
  not not_8 (not_8_out, A7A6A5A4A3A2A1A0[7]);
  Multiplexer #(.select(2), .enable("false")) multiplexer_1 (
    .in0(and_1_out), .in1(or_1_out), .in2(xor_1_out), .in3(not_1_out), .out(E7E6E5E4E3E2E1E0[0]), .sel(S1S0));
  Multiplexer #(.select(2), .enable("false")) multiplexer_2 (
    .in0(and_2_out), .in1(or_2_out), .in2(xor_2_out), .in3(not_2_out), .out(E7E6E5E4E3E2E1E0[1]), .sel(S1S0));
  Multiplexer #(.select(2), .enable("false")) multiplexer_3 (
    .in0(and_3_out), .in1(or_3_out), .in2(xor_3_out), .in3(not_3_out), .out(E7E6E5E4E3E2E1E0[2]), .sel(S1S0));
  Multiplexer #(.select(2), .enable("false")) multiplexer_4 (
    .in0(and_4_out), .in1(or_4_out), .in2(xor_4_out), .in3(not_4_out), .out(E7E6E5E4E3E2E1E0[3]), .sel(S1S0));
  Multiplexer #(.select(2), .enable("false")) multiplexer_5 (
    .in0(and_5_out), .in1(or_5_out), .in2(xor_5_out), .in3(not_5_out), .out(E7E6E5E4E3E2E1E0[4]), .sel(S1S0));
  Multiplexer #(.select(2), .enable("false")) multiplexer_6 (
    .in0(and_6_out), .in1(or_6_out), .in2(xor_6_out), .in3(not_6_out), .out(E7E6E5E4E3E2E1E0[5]), .sel(S1S0));
  Multiplexer #(.select(2), .enable("false")) multiplexer_7 (
    .in0(and_7_out), .in1(or_7_out), .in2(xor_7_out), .in3(not_7_out), .out(E7E6E5E4E3E2E1E0[6]), .sel(S1S0));
  Multiplexer #(.select(2), .enable("false")) multiplexer_8 (
    .in0(and_8_out), .in1(or_8_out), .in2(xor_8_out), .in3(not_8_out), .out(E7E6E5E4E3E2E1E0[7]), .sel(S1S0));

  // Notes on the sheet:
  //   23CS081
endmodule

module one_bit_sixteen_logical (
  input  B0,
  input  A0,
  input  [3:0] S3S2S1S0,
  output E0
);

  wire and_1_out, and_2_out, and_3_out, nand_1_out, not_1_out, not_2_out, not_3_out, or_1_out, or_2_out,
       or_3_out, xnor_1_out, xor_1_out;

  not not_1 (not_1_out, B0);
  not not_2 (not_2_out, A0);
  xnor xnor_1 (xnor_1_out, A0, B0);
  or or_1 (or_1_out, A0, not_1_out);
  and and_1 (and_1_out, A0, B0);
  and and_2 (and_2_out, A0, not_1_out);
  and and_3 (and_3_out, not_2_out, B0);
  xor xor_1 (xor_1_out, A0, B0);
  not not_3 (not_3_out, or_2_out);
  or or_2 (or_2_out, A0, B0);
  or or_3 (or_3_out, not_2_out, B0);
  nand nand_1 (nand_1_out, A0, B0);
  Multiplexer #(.select(4), .enable("false")) multiplexer_1 (
    .in0(1'b0), .in1(and_1_out), .in2(and_2_out), .in3(A0), .in4(and_3_out), .in5(B0), .in6(xor_1_out),
    .in7(or_2_out), .in8(not_3_out), .in9(xnor_1_out), .in10(not_1_out), .in11(or_1_out), .in12(not_2_out),
    .in13(or_3_out), .in14(nand_1_out), .in15(1'b1), .out(E0), .sel(S3S2S1S0));

  // Notes on the sheet:
  //   23CS081
endmodule

module two_bit_sixteen_logical (
  input  [1:0] B1B0,
  input  [1:0] A1A0,
  input  [3:0] S3S2S1S0,
  output [1:0] B1B0_2
);

  wire and_1_out, and_2_out, and_3_out, and_4_out, and_5_out, and_6_out, nand_1_out, nand_2_out, not_1_out,
       not_2_out, not_3_out, not_4_out, not_5_out, not_6_out, or_1_out, or_2_out, or_3_out, or_4_out,
       or_5_out, or_6_out, xnor_1_out, xnor_2_out, xor_1_out, xor_2_out;

  not not_1 (not_1_out, B1B0[0]);
  not not_2 (not_2_out, B1B0[1]);
  not not_3 (not_3_out, A1A0[0]);
  not not_4 (not_4_out, A1A0[1]);
  and and_1 (and_1_out, A1A0[0], B1B0[0]);
  and and_2 (and_2_out, A1A0[0], not_1_out);
  and and_3 (and_3_out, not_3_out, B1B0[0]);
  xor xor_1 (xor_1_out, A1A0[0], B1B0[0]);
  or or_1 (or_1_out, A1A0[0], B1B0[0]);
  xnor xnor_1 (xnor_1_out, A1A0[0], B1B0[0]);
  or or_2 (or_2_out, A1A0[0], not_1_out);
  and and_4 (and_4_out, A1A0[1], B1B0[1]);
  and and_5 (and_5_out, A1A0[1], not_2_out);
  and and_6 (and_6_out, not_4_out, B1B0[1]);
  xor xor_2 (xor_2_out, A1A0[1], B1B0[1]);
  or or_3 (or_3_out, A1A0[1], B1B0[1]);
  xnor xnor_2 (xnor_2_out, A1A0[1], B1B0[1]);
  or or_4 (or_4_out, A1A0[1], not_2_out);
  not not_5 (not_5_out, or_1_out);
  or or_5 (or_5_out, not_3_out, B1B0[0]);
  nand nand_1 (nand_1_out, A1A0[0], B1B0[0]);
  not not_6 (not_6_out, or_3_out);
  or or_6 (or_6_out, not_4_out, B1B0[1]);
  nand nand_2 (nand_2_out, A1A0[1], B1B0[1]);
  Multiplexer #(.select(4), .enable("false")) multiplexer_1 (
    .in0(1'b0), .in1(and_1_out), .in2(and_2_out), .in3(A1A0[0]), .in4(and_3_out), .in5(B1B0[0]),
    .in6(xor_1_out), .in7(or_1_out), .in8(not_5_out), .in9(xnor_1_out), .in10(not_1_out), .in11(or_2_out),
    .in12(not_3_out), .in13(or_5_out), .in14(nand_1_out), .in15(1'b1), .out(B1B0_2[0]), .sel(S3S2S1S0));
  Multiplexer #(.select(4), .enable("false")) multiplexer_2 (
    .in0(1'b0), .in1(and_4_out), .in2(and_5_out), .in3(A1A0[1]), .in4(and_6_out), .in5(B1B0[1]),
    .in6(xor_2_out), .in7(or_3_out), .in8(not_6_out), .in9(xnor_2_out), .in10(not_2_out), .in11(or_4_out),
    .in12(not_4_out), .in13(or_6_out), .in14(nand_2_out), .in15(1'b1), .out(B1B0_2[1]), .sel(S3S2S1S0));

  // Notes on the sheet:
  //   23CS081
endmodule

module two_bit_bidirectional_shifter (
  input  [1:0] A1A0,
  input  IR,
  input  IL,
  input  SELECT,
  output [1:0] O1O0
);

  Multiplexer #(.enable("false")) multiplexer_1 (.in0(IR), .in1(A1A0[0]), .out(O1O0[1]), .sel(SELECT));
  Multiplexer #(.enable("false")) multiplexer_2 (.in0(A1A0[1]), .in1(IL), .out(O1O0[0]), .sel(SELECT));

  // Notes on the sheet:
  //   SELECT 1: LEFT
  //   23CS081
  //   SELECT 0 : RIGHT
  //   bit 1
  //   bit 0
endmodule

module four_bit_bidirectional_shifter (
  input  [3:0] in_1,
  input  IL,
  input  IR,
  input  SELECT,
  output [3:0] O3O2O1O0
);

  Multiplexer #(.enable("false")) multiplexer_1 (.in0(IR), .in1(in_1[2]), .out(O3O2O1O0[3]), .sel(SELECT));
  Multiplexer #(.enable("false")) multiplexer_2 (.in0(in_1[3]), .in1(in_1[1]), .out(O3O2O1O0[2]), .sel(SELECT));
  Multiplexer #(.enable("false")) multiplexer_3 (.in0(in_1[2]), .in1(in_1[0]), .out(O3O2O1O0[1]), .sel(SELECT));
  Multiplexer #(.enable("false")) multiplexer_4 (.in0(in_1[1]), .in1(IL), .out(O3O2O1O0[0]), .sel(SELECT));

  // Notes on the sheet:
  //   SELECT 0 : RIGHT
  //   SELECT 1: LEFT
  //   23CS081
  //   bit 3
  //   bit 2
  //   bit 1
  //   bit 0
endmodule

module eight_bit_bidirectional_shifter (
  input  SELECT,
  input  IR,
  input  [7:0] A6A5A4A3A2A1A0,
  input  IL,
  output [7:0] E6E5E4E3E2E1E0
);

  Multiplexer #(.enable("false")) multiplexer_1 (
    .in0(IR), .in1(A6A5A4A3A2A1A0[6]), .out(E6E5E4E3E2E1E0[7]), .sel(SELECT));
  Multiplexer #(.enable("false")) multiplexer_2 (
    .in0(A6A5A4A3A2A1A0[7]), .in1(A6A5A4A3A2A1A0[5]), .out(E6E5E4E3E2E1E0[6]), .sel(SELECT));
  Multiplexer #(.enable("false")) multiplexer_3 (
    .in0(A6A5A4A3A2A1A0[6]), .in1(A6A5A4A3A2A1A0[4]), .out(E6E5E4E3E2E1E0[5]), .sel(SELECT));
  Multiplexer #(.enable("false")) multiplexer_4 (
    .in0(A6A5A4A3A2A1A0[5]), .in1(A6A5A4A3A2A1A0[3]), .out(E6E5E4E3E2E1E0[4]), .sel(SELECT));
  Multiplexer #(.enable("false")) multiplexer_5 (
    .in0(A6A5A4A3A2A1A0[4]), .in1(A6A5A4A3A2A1A0[2]), .out(E6E5E4E3E2E1E0[3]), .sel(SELECT));
  Multiplexer #(.enable("false")) multiplexer_6 (
    .in0(A6A5A4A3A2A1A0[3]), .in1(A6A5A4A3A2A1A0[1]), .out(E6E5E4E3E2E1E0[2]), .sel(SELECT));
  Multiplexer #(.enable("false")) multiplexer_7 (
    .in0(A6A5A4A3A2A1A0[2]), .in1(A6A5A4A3A2A1A0[0]), .out(E6E5E4E3E2E1E0[1]), .sel(SELECT));
  Multiplexer #(.enable("false")) multiplexer_8 (
    .in0(A6A5A4A3A2A1A0[1]), .in1(IL), .out(E6E5E4E3E2E1E0[0]), .sel(SELECT));

  // Notes on the sheet:
  //   SELECT 0 : RIGHT
  //   SELECT 1: LEFT
  //   bit 7
  //   bit 6
  //   bit 5
  //   bit 4
  //   bit 3
  //   bit 2
  //   bit 1
  //   bit 0
endmodule

module one_bit_ALU (
  input  B0,
  input  A0,
  input  Cin,
  input  IR,
  input  IL,
  input  [1:0] S1S0,
  input  [1:0] S3S2,
  output Cout,
  output F0
);

  wire bit_0_Arith_d0, bit_0_Logic_e0;

  one_bit_arithmetic bit_0_Arith (.Cin(Cin), .A0(A0), .B0(B0), .D0(bit_0_Arith_d0), .Cout(Cout), .S1S0(S1S0));
  one_bit_logical bit_0_Logic (.B0(B0), .A0(A0), .S1S0(S1S0), .E0(bit_0_Logic_e0));
  Multiplexer #(.select(2), .enable("false")) multiplexer_1 (
    .in0(bit_0_Arith_d0), .in1(bit_0_Logic_e0), .in2(IR), .in3(IL), .out(F0), .sel(S3S2));

  // Notes on the sheet:
  //   23CS081
endmodule

module two_bit_ALU (
  input  [1:0] B1B0,
  input  [1:0] A1A0,
  input  Cin,
  input  IR,
  input  IL,
  input  [1:0] S1S0,
  input  [1:0] S3S2,
  output [1:0] F1F0,
  output Cout
);

  wire bit_0_Arith_cout, bit_0_Arith_d0, bit_0_Logic_e0, bit_1_Arith_d0, bit_1_Logic_e0;

  one_bit_arithmetic bit_0_Arith (
    .Cin(Cin), .A0(A1A0[0]), .B0(B1B0[0]), .D0(bit_0_Arith_d0), .Cout(bit_0_Arith_cout), .S1S0(S1S0));
  one_bit_logical bit_0_Logic (.B0(B1B0[0]), .A0(A1A0[0]), .S1S0(S1S0), .E0(bit_0_Logic_e0));
  one_bit_arithmetic bit_1_Arith (
    .Cin(bit_0_Arith_cout), .A0(A1A0[1]), .B0(B1B0[1]), .D0(bit_1_Arith_d0), .Cout(Cout), .S1S0(S1S0));
  one_bit_logical bit_1_Logic (.B0(B1B0[1]), .A0(A1A0[1]), .S1S0(S1S0), .E0(bit_1_Logic_e0));
  Multiplexer #(.select(2), .enable("false")) multiplexer_1 (
    .in0(bit_0_Arith_d0), .in1(bit_0_Logic_e0), .in2(A1A0[1]), .in3(IL), .out(F1F0[0]), .sel(S3S2));
  Multiplexer #(.select(2), .enable("false")) multiplexer_2 (
    .in0(bit_1_Arith_d0), .in1(bit_1_Logic_e0), .in2(IR), .in3(A1A0[0]), .out(F1F0[1]), .sel(S3S2));

  // Notes on the sheet:
  //   23CS081
endmodule

module four_bit_ALU (
  input  [3:0] B1B0,
  input  [3:0] A1A0,
  input  Cin,
  input  IR,
  input  IL,
  input  [1:0] S1S0,
  input  [1:0] S3S2,
  output [3:0] F1F0,
  output Cout
);

  wire bit_0_Arith_cout, bit_0_Arith_d0, bit_0_Logic_e0, bit_1_Arith_cout, bit_1_Arith_d0, bit_1_Logic_e0,
       bit_2_Arith_cout, bit_2_Arith_d0, bit_2_Logic_e0, bit_3_Arith_d0, bit_3_Logic_e0;

  one_bit_arithmetic bit_0_Arith (
    .Cin(Cin), .A0(A1A0[0]), .B0(B1B0[0]), .D0(bit_0_Arith_d0), .Cout(bit_0_Arith_cout), .S1S0(S1S0));
  one_bit_logical bit_0_Logic (.B0(B1B0[0]), .A0(A1A0[0]), .S1S0(S1S0), .E0(bit_0_Logic_e0));
  one_bit_arithmetic bit_1_Arith (
    .Cin(bit_0_Arith_cout), .A0(A1A0[1]), .B0(B1B0[1]), .D0(bit_1_Arith_d0), .Cout(bit_1_Arith_cout),
    .S1S0(S1S0));
  one_bit_logical bit_1_Logic (.B0(B1B0[1]), .A0(A1A0[1]), .S1S0(S1S0), .E0(bit_1_Logic_e0));
  one_bit_arithmetic bit_2_Arith (
    .Cin(bit_1_Arith_cout), .A0(A1A0[2]), .B0(B1B0[2]), .D0(bit_2_Arith_d0), .Cout(bit_2_Arith_cout),
    .S1S0(S1S0));
  one_bit_logical bit_2_Logic (.B0(B1B0[2]), .A0(A1A0[2]), .S1S0(S1S0), .E0(bit_2_Logic_e0));
  one_bit_arithmetic bit_3_Arith (
    .Cin(bit_2_Arith_cout), .A0(A1A0[3]), .B0(B1B0[3]), .D0(bit_3_Arith_d0), .Cout(Cout), .S1S0(S1S0));
  one_bit_logical bit_3_Logic (.B0(B1B0[3]), .A0(A1A0[3]), .S1S0(S1S0), .E0(bit_3_Logic_e0));
  Multiplexer #(.select(2), .enable("false")) multiplexer_1 (
    .in0(bit_0_Arith_d0), .in1(bit_0_Logic_e0), .in2(A1A0[0]), .in3(IL), .out(F1F0[0]), .sel(S3S2));
  Multiplexer #(.select(2), .enable("false")) multiplexer_2 (
    .in0(bit_1_Arith_d0), .in1(bit_1_Logic_e0), .in2(IR), .in3(A1A0[0]), .out(F1F0[1]), .sel(S3S2));
  Multiplexer #(.select(2), .enable("false")) multiplexer_3 (
    .in0(bit_2_Arith_d0), .in1(bit_2_Logic_e0), .in2(A1A0[3]), .in3(A1A0[1]), .out(F1F0[2]), .sel(S3S2));
  Multiplexer #(.select(2), .enable("false")) multiplexer_4 (
    .in0(bit_3_Arith_d0), .in1(bit_3_Logic_e0), .in2(IR), .in3(A1A0[2]), .out(F1F0[3]), .sel(S3S2));

  // Notes on the sheet:
  //   23CS081
  //   Bit-0
  //   Bit 1
  //   Bit 2
  //   Bit 3
endmodule

module eight_bit_ALU (
  input  [7:0] B,
  input  [7:0] A,
  input  Cin,
  input  IL,
  input  IR,
  input  [1:0] S1S0,
  input  [1:0] S3S2,
  output [7:0] AC,
  output Cout
);

  wire bit_0_Arith_cout, bit_0_Arith_d0, bit_0_Logic_e0, bit_1_Arith_cout, bit_1_Arith_d0, bit_1_Logic_e0,
       bit_2_Arith_cout, bit_2_Arith_d0, bit_2_Logic_e0, bit_3_Arith_cout, bit_3_Arith_d0, bit_3_Logic_e0,
       bit_4_Arith_cout, bit_4_Arith_d0, bit_4_Logic_e0, bit_5_Arith_cout, bit_5_Arith_d0, bit_5_Logic_e0,
       bit_6_Arith_cout, bit_6_Arith_d0, bit_6_Logic_e0, bit_7_Arith_d0, bit_7_Logic_e0;

  one_bit_arithmetic bit_0_Arith (
    .Cin(Cin), .A0(A[0]), .B0(B[0]), .D0(bit_0_Arith_d0), .Cout(bit_0_Arith_cout), .S1S0(S1S0));
  one_bit_logical bit_0_Logic (.B0(B[0]), .A0(A[0]), .S1S0(S1S0), .E0(bit_0_Logic_e0));
  one_bit_arithmetic bit_1_Arith (
    .Cin(bit_0_Arith_cout), .A0(A[1]), .B0(B[1]), .D0(bit_1_Arith_d0), .Cout(bit_1_Arith_cout), .S1S0(S1S0));
  one_bit_logical bit_1_Logic (.B0(B[1]), .A0(A[1]), .S1S0(S1S0), .E0(bit_1_Logic_e0));
  one_bit_arithmetic bit_2_Arith (
    .Cin(bit_1_Arith_cout), .A0(A[2]), .B0(B[2]), .D0(bit_2_Arith_d0), .Cout(bit_2_Arith_cout), .S1S0(S1S0));
  one_bit_logical bit_2_Logic (.B0(B[2]), .A0(A[2]), .S1S0(S1S0), .E0(bit_2_Logic_e0));
  one_bit_arithmetic bit_3_Arith (
    .Cin(bit_2_Arith_cout), .A0(A[3]), .B0(B[3]), .D0(bit_3_Arith_d0), .Cout(bit_3_Arith_cout), .S1S0(S1S0));
  one_bit_logical bit_3_Logic (.B0(B[3]), .A0(A[3]), .S1S0(S1S0), .E0(bit_3_Logic_e0));
  one_bit_arithmetic bit_4_Arith (
    .Cin(bit_3_Arith_cout), .A0(A[4]), .B0(B[4]), .D0(bit_4_Arith_d0), .Cout(bit_4_Arith_cout), .S1S0(S1S0));
  one_bit_logical bit_4_Logic (.B0(B[4]), .A0(A[4]), .S1S0(S1S0), .E0(bit_4_Logic_e0));
  one_bit_arithmetic bit_5_Arith (
    .Cin(bit_4_Arith_cout), .A0(A[5]), .B0(B[5]), .D0(bit_5_Arith_d0), .Cout(bit_5_Arith_cout), .S1S0(S1S0));
  one_bit_logical bit_5_Logic (.B0(B[5]), .A0(A[5]), .S1S0(S1S0), .E0(bit_5_Logic_e0));
  one_bit_arithmetic bit_6_Arith (
    .Cin(bit_5_Arith_cout), .A0(A[6]), .B0(B[6]), .D0(bit_6_Arith_d0), .Cout(bit_6_Arith_cout), .S1S0(S1S0));
  one_bit_logical bit_6_Logic (.B0(B[6]), .A0(A[6]), .S1S0(S1S0), .E0(bit_6_Logic_e0));
  one_bit_arithmetic bit_7_Arith (
    .Cin(bit_6_Arith_cout), .A0(A[7]), .B0(B[7]), .D0(bit_7_Arith_d0), .Cout(Cout), .S1S0(S1S0));
  one_bit_logical bit_7_Logic (.B0(B[7]), .A0(A[7]), .S1S0(S1S0), .E0(bit_7_Logic_e0));
  Multiplexer #(.select(2), .enable("false")) multiplexer_1 (
    .in0(bit_0_Arith_d0), .in1(bit_0_Logic_e0), .in2(A[1]), .in3(IR), .out(AC[0]), .sel(S3S2));
  Multiplexer #(.select(2), .enable("false")) multiplexer_2 (
    .in0(bit_1_Arith_d0), .in1(bit_1_Logic_e0), .in2(A[2]), .in3(A[0]), .out(AC[1]), .sel(S3S2));
  Multiplexer #(.select(2), .enable("false")) multiplexer_3 (
    .in0(bit_2_Arith_d0), .in1(bit_2_Logic_e0), .in2(A[3]), .in3(A[1]), .out(AC[2]), .sel(S3S2));
  Multiplexer #(.select(2), .enable("false")) multiplexer_4 (
    .in0(bit_3_Arith_d0), .in1(bit_3_Logic_e0), .in2(A[4]), .in3(A[2]), .out(AC[3]), .sel(S3S2));
  Multiplexer #(.select(2), .enable("false")) multiplexer_5 (
    .in0(bit_4_Arith_d0), .in1(bit_4_Logic_e0), .in2(A[4]), .in3(A[3]), .out(AC[4]), .sel(S3S2));
  Multiplexer #(.select(2), .enable("false")) multiplexer_6 (
    .in0(bit_5_Arith_d0), .in1(bit_5_Logic_e0), .in2(A[6]), .in3(A[4]), .out(AC[5]), .sel(S3S2));
  Multiplexer #(.select(2), .enable("false")) multiplexer_7 (
    .in0(bit_6_Arith_d0), .in1(bit_6_Logic_e0), .in2(A[7]), .in3(A[5]), .out(AC[6]), .sel(S3S2));
  Multiplexer #(.select(2), .enable("false")) multiplexer_8 (
    .in0(bit_7_Arith_d0), .in1(bit_7_Logic_e0), .in2(IL), .in3(A[6]), .out(AC[7]), .sel(S3S2));

  // Notes on the sheet:
  //   23CS081
  //   Bit-0
  //   Bit 1
  //   Bit 2
  //   Bit 3
  //   Bit-4
  //   Bit 5
  //   Bit 6
  //   Bit 7
endmodule

module sixteen_bit_ALU (
  input  [1:0] S0S1,
  input  [1:0] S2S3,
  input  IL,
  input  Cin,
  input  [15:0] A,
  input  [15:0] B,
  input  IR,
  output [15:0] AC,
  output Cout
);

  wire Bit_0_to_7_cout;

  eight_bit_ALU Bit_0_to_7 (
    .B(B[7:0]), .A(A[7:0]), .Cin(Cin), .IL(IL), .IR(A[8]), .Cout(Bit_0_to_7_cout), .S1S0(S0S1), .S3S2(S2S3),
    .AC(AC[7:0]));
  eight_bit_ALU Bit_8_to_15 (
    .B(B[15:8]), .A(A[15:8]), .Cin(Bit_0_to_7_cout), .IL(A[7]), .IR(IR), .Cout(Cout), .S1S0(S0S1),
    .S3S2(S2S3), .AC(AC[15:8]));

  // Notes on the sheet:
  //   23CS081
endmodule

module commonBusSystem (
  input  [11:0] MEM_AR,
  input  MEM_AR_SEL,
  input  [15:0] MEM_DATA,
  input  MEM_WR,
  input  MEM_DATA_SEL,
  input  MEM_CLR,
  input  MEM_CS,
  input  MEM_LD,
  input  LD_AR,
  input  INR_AR,
  input  CLR_AR,
  input  LD_PC,
  input  INR_PC,
  input  CLR_PC,
  input  [2:0] S2S1S0,
  input  LD_DR,
  input  INR_DR,
  input  IL,
  input  CLR_DR,
  input  Cin,
  input  [1:0] S2S3,
  input  [1:0] S0S1,
  input  LD_AC,
  input  [1:0] SEL_1,
  input  INR_AC,
  input  CLR_AC,
  input  [1:0] SEL_2,
  input  IR,
  input  [7:0] INPR,
  input  LD_IR,
  input  CLR_IR,
  input  LD_TR,
  input  INR_TR,
  input  CLR_TR,
  input  INR_OUTR,
  input  CLR_OUTR,
  input  in_37,
  output Cout
);

  wire CLK_SYSTEM_2_out, CLK_SYSTEM_out, MEM_CLK_out;
  wire [11:0] AR_q, multiplexer_1_out, PC_q;
  wire [15:0] AC_q, ALU_ac, CB_q, DR_q, IR_q, multiplexer_2_out, multiplexer_3_out, multiplexer_4_out,
       multiplexer_5_out, ram_1_data, TR_q;
  wire [15:8] undriven;

  Multiplexer #(.width(12), .enable("false")) multiplexer_1 (
    .in0(AR_q), .in1(MEM_AR), .out(multiplexer_1_out), .sel(MEM_AR_SEL));
  Multiplexer #(.width(16), .enable("false")) multiplexer_2 (
    .in0(multiplexer_5_out), .in1(MEM_DATA), .out(multiplexer_2_out), .sel(MEM_DATA_SEL));
  Multiplexer #(.select(2), .width(16), .enable("false")) multiplexer_3 (
    .in0(AC_q), .in1(DR_q), .in2({undriven, INPR}), .in3(AC_q), .out(multiplexer_3_out), .sel(SEL_1));
  Multiplexer #(.select(2), .width(16), .enable("false")) multiplexer_4 (
    .in0(AC_q), .in1(DR_q), .in2({undriven, INPR}), .in3(AC_q), .out(multiplexer_4_out), .sel(SEL_2));
  sixteen_bit_ALU ALU (
    .S0S1(S0S1), .S2S3(S2S3), .IL(IL), .Cin(Cin), .A(multiplexer_3_out), .B(multiplexer_4_out), .IR(IR),
    .AC(ALU_ac), .Cout(Cout));
  Clock MEM_CLK (.out(MEM_CLK_out));
  Counter #(.width(12), .max('hfff)) AR (
    .load(LD_AR), .D(multiplexer_5_out[11:0]), .count(INR_AR), .Q(AR_q), .clk(CLK_SYSTEM_out), .clr(CLR_AR));  // open: carry
  Counter #(.width(12), .max('hfff)) PC (
    .load(LD_PC), .D(multiplexer_5_out[11:0]), .count(INR_PC), .Q(PC_q), .clk(CLK_SYSTEM_out), .clr(CLR_PC));  // open: carry
  Counter #(.width(16), .max('hffff)) DR (
    .load(LD_DR), .D(multiplexer_5_out), .count(INR_DR), .Q(DR_q), .clk(CLK_SYSTEM_out), .clr(CLR_DR));  // open: carry
  Counter #(.width(16), .max('hffff)) AC (
    .load(LD_AC), .D(ALU_ac), .count(INR_AC), .Q(AC_q), .clk(CLK_SYSTEM_out), .clr(CLR_AC));  // open: carry
  Register #(.width(16)) u_IR (.D(multiplexer_5_out), .en(LD_IR), .Q(IR_q), .clk(CLK_SYSTEM_out), .clr(CLR_IR));
  Counter #(.width(16), .max('hffff)) TR (
    .load(LD_TR), .D(multiplexer_5_out), .count(INR_TR), .Q(TR_q), .clk(CLK_SYSTEM_out), .clr(CLR_TR));  // open: carry
  Register OUTR (.D(multiplexer_5_out[7:0]), .en(INR_OUTR), .clk(CLK_SYSTEM_out), .clr(CLR_OUTR));  // open: Q
  RAM #(.addrWidth(12), .dataWidth(16), .bus("separate")) ram_1 (
    .addr(multiplexer_1_out), .din(multiplexer_2_out), .data(ram_1_data), .str(MEM_WR), .sel(MEM_CS),
    .clk(MEM_CLK_out), .ld(MEM_LD), .clr(MEM_CLR));
  Clock CLK_SYSTEM (.out(CLK_SYSTEM_out));
  Multiplexer #(.select(3), .width(16), .enable("false")) multiplexer_5 (
    .in1({4'b0000, AR_q}), .in2({4'b0000, PC_q}), .in3(DR_q), .in4(AC_q), .in5(IR_q), .in6(TR_q),
    .in7(ram_1_data), .out(multiplexer_5_out), .sel(S2S1S0));  // open: in0
  Register #(.width(16)) CB (.D(multiplexer_5_out), .en(1'b1), .Q(CB_q), .clk(CLK_SYSTEM_2_out), .clr(1'b0));
  Clock CLK_SYSTEM_2 (.out(CLK_SYSTEM_2_out));

  // Notes on the sheet:
  //   23CS081
endmodule
